// Logisim project task1.circ as structural Verilog: 2 circuits, main circuit main
module main (
  input  in_1,
  input  in_2,
  input  in_3,
  output out_4,
  output out_5
);

  wire and_1_out, and_2_out, and_3_out, and_4_out, and_5_out, and_6_out, and_7_out, not_1_out, not_2_out,
       not_3_out;

  not not_1 (not_1_out, in_2);
  not not_2 (not_2_out, in_3);
  not not_3 (not_3_out, in_1);
  and and_1 (and_1_out, not_1_out, not_2_out, in_1);
  and and_2 (and_2_out, not_1_out, in_3, not_3_out);
  and and_3 (and_3_out, in_2, not_2_out, not_3_out);
  and and_4 (and_4_out, in_2, in_3, in_1);
  and and_5 (and_5_out, in_2, in_1);
  and and_6 (and_6_out, in_2, in_3);
  and and_7 (and_7_out, in_3, in_1);
  or or_1 (out_5, and_5_out, and_6_out, and_7_out);
  or or_2 (out_4, and_1_out, and_2_out, and_3_out, and_4_out);
endmodule

module adder_schema (
  input  [7:0] in_1,
  input  [7:0] in_2,
  output [7:0] out_3
);

  wire main_1_out_5, main_2_out_5, main_3_out_5, main_4_out_5, main_5_out_5, main_6_out_5, main_7_out_5,
       main_8_out_5;

  // Probe on in_1
  // Probe on in_2
  main main_1 (.in_1(main_8_out_5), .in_2(in_1[0]), .in_3(in_2[0]), .out_4(out_3[0]), .out_5(main_1_out_5));
  main main_2 (.in_1(main_1_out_5), .in_2(in_1[1]), .in_3(in_2[1]), .out_4(out_3[1]), .out_5(main_2_out_5));
  main main_3 (.in_1(main_2_out_5), .in_2(in_1[2]), .in_3(in_2[2]), .out_4(out_3[2]), .out_5(main_3_out_5));
  main main_4 (.in_1(main_3_out_5), .in_2(in_1[3]), .in_3(in_2[3]), .out_4(out_3[3]), .out_5(main_4_out_5));
  main main_5 (.in_1(main_4_out_5), .in_2(in_1[4]), .in_3(in_2[4]), .out_4(out_3[4]), .out_5(main_5_out_5));
  main main_6 (.in_1(main_5_out_5), .in_2(in_1[5]), .in_3(in_2[5]), .out_4(out_3[5]), .out_5(main_6_out_5));
  main main_7 (.in_1(main_6_out_5), .in_2(in_1[6]), .in_3(in_2[6]), .out_4(out_3[6]), .out_5(main_7_out_5));
  main main_8 (.in_1(main_7_out_5), .in_2(in_1[7]), .in_3(in_2[7]), .out_4(out_3[7]), .out_5(main_8_out_5));
  // Probe on out_3
endmodule
