// Logisim project task2.circ as structural Verilog: 1 circuit, main circuit main
module main (
  input  x1,
  input  x2,
  input  x3,
  input  x4,
  output y1,
  output y2,
  output y3,
  output y4
);

  wire and_1_out, and_2_out, and_3_out, and_4_out, and_5_out, and_6_out, and_7_out, and_8_out, and_9_out,
       and_10_out, and_11_out, not_1_out, not_2_out, not_3_out, not_4_out;

  not not_1 (not_1_out, x1);
  not not_2 (not_2_out, x2);
  not not_3 (not_3_out, x3);
  not not_4 (not_4_out, x4);
  and and_1 (and_1_out, not_1_out, not_2_out);
  and and_2 (and_2_out, not_1_out, not_3_out);
  and and_3 (and_3_out, not_1_out, not_4_out);
  and and_4 (and_4_out, not_1_out, x2, not_3_out);
  and and_5 (and_5_out, not_1_out, x2, not_4_out);
  and and_6 (and_6_out, not_1_out, not_2_out, x3, x4);
  and and_7 (and_7_out, not_1_out, not_3_out, x4);
  and and_8 (and_8_out, not_1_out, x3, not_4_out);
  and and_9 (and_9_out, not_2_out, not_3_out, x4);
  and and_10 (and_10_out, not_1_out, not_4_out);
  and and_11 (and_11_out, x1, not_2_out, not_3_out);
  or or_1 (y1, and_1_out, and_2_out, and_3_out);
  or or_2 (y2, and_4_out, and_5_out, and_6_out);
  or or_3 (y3, and_7_out, and_8_out, and_9_out);
  or or_4 (y4, and_10_out, and_11_out);
endmodule
